// Logisim project alu.circ as structural Verilog: 13 circuits, main circuit main
module main (
  input  [31:0] X,
  input  [31:0] Y,
  input  [3:0] Switch,
  output Signed_Overflow,
  output Equal,
  output [31:0] Result
);

  wire equal0, equal1, equal2, equal3, equal4, equal5, equal6, equal7, equal8, equal9, equal10, equal11,
       overflow0, overflow1, overflow2, overflow3, overflow4, overflow5, overflow6, overflow7, overflow8,
       overflow9, overflow10, overflow11;
  wire [31:0] result0, result1, result2, result3, result4, result5, result6, result7, result8, result9,
       result10, result11;

  sll sll (.X(X), .Y(Y), .Signed_Overflow(overflow0), .Equal(equal0), .Result(result0));
  srl srl (.X(X), .Y(Y), .Signed_Overflow(overflow1), .Equal(equal1), .Result(result1));
  sra sra (.X(X), .Y(Y), .Signed_Overflow(overflow2), .Equal(equal2), .Result(result2));
  add add (.X(X), .Y(Y), .Signed_Overflow(overflow3), .Equal(equal3), .Result(result3));
  addu addu (.X(X), .Y(Y), .Signed_Overflow(overflow4), .Equal(equal4), .Result(result4));
  sub sub (.X(X), .Y(Y), .Signed_Overflow(overflow5), .Equal(equal5), .Result(result5));
  subu subu (.X(X), .Y(Y), .Signed_Overflow(overflow6), .Equal(equal6), .Result(result6));
  \and  \and  (.X(X), .Y(Y), .Signed_Overflow(overflow7), .Equal(equal7), .Result(result7));
  \or  \or  (.X(X), .Y(Y), .Signed_Overflow(overflow8), .Equal(equal8), .Result(result8));
  \xor  \xor  (.X(X), .Y(Y), .Signed_Overflow(overflow9), .Equal(equal9), .Result(result9));
  slt slt (.X(X), .Y(Y), .Signed_Overflow(overflow10), .Equal(equal10), .Result(result10));
  sltu slt_2 (.X(X), .Y(Y), .Signed_Overflow(overflow11), .Equal(equal11), .Result(result11));
  Multiplexer #(.select(4), .enable("false")) multiplexer_1 (
    .in0(overflow0), .in1(overflow1), .in2(overflow2), .in3(overflow3), .in4(overflow4), .in5(overflow5),
    .in6(overflow6), .in7(overflow7), .in8(overflow8), .in9(overflow9), .in10(overflow10), .in11(overflow11),
    .in12(1'b0), .in13(1'b0), .in14(1'b0), .in15(1'b0), .out(Signed_Overflow), .sel(Switch));
  Multiplexer #(.select(4), .enable("false")) multiplexer_2 (
    .in0(equal0), .in1(equal1), .in2(equal2), .in3(equal3), .in4(equal4), .in5(equal5), .in6(equal6),
    .in7(equal7), .in8(equal8), .in9(equal9), .in10(equal10), .in11(equal11), .in12(1'b0), .in13(1'b0),
    .in14(1'b0), .in15(1'b0), .out(Equal), .sel(Switch));
  Multiplexer #(.select(4), .width(32), .enable("false")) multiplexer_3 (
    .in0(result0), .in1(result1), .in2(result2), .in3(result3), .in4(result4), .in5(result5), .in6(result6),
    .in7(result7), .in8(result8), .in9(result9), .in10(result10), .in11(result11), .in12({32{1'b0}}),
    .in13({32{1'b0}}), .in14({32{1'b0}}), .in15({32{1'b0}}), .out(Result), .sel(Switch));

  // Other names for the same wires on the sheet: overflow = Signed_Overflow; S[3:0] = Switch

  // Notes on the sheet:
  //   INPUTS to your circuit
  //   X = first operand
  //   Switch = determine action
  //   Y = second operand
  //   DON'T CHANGE THE LOCATIONS OF THE INPUTS AND OUTPUTS!
  //   Switch Key:
  //   0 | sll | Y << X | 0
  //   4 | addu | X + Y | 0
  //   6 | subu | X - Y | 0
  //   8 | or | X OR Y | 0
  //   OUTPUTS from your circuit
  //   Equal : 1 iff X==Y
  //   Result = result of op
  //   2 | sra | Y >>> X | 0
  //   SignO: 1 iff operation +/- and there was signO
  //   Switch | Operation Name | Result | Signed Overflow
  //   1 | srl | Y >> X | 0
  //   10 | slt (signed comp) | ( X < Y) ? 1 : 0 | 0
  //   11 | sltu (unsighed comp) | (X < Y) ? 1 : 0 | 0
  //   slt == 0xFFFFFFFF < 0x0000000 is 1
  //   sltu == 0xFFFFFFFF < 0x00000000 is 0
  //   3 | add | X + Y | 1 iff overflow
  //   5 | sub | X - Y | 1 iff overflow
  //   7 | and | X AND Y | 0
  //   9 | xor | X XOR Y | 0
endmodule

module sll (
  input  [31:0] X,
  input  [31:0] Y,
  output Signed_Overflow,
  output Equal,
  output [31:0] Result
);

  Shifter #(.width(32)) shifter_1 (.in(Y), .\dist (X[4:0]), .out(Result));
  Comparator #(.width(32)) comparator_1 (.a(Y), .b(X), .eq(Equal));  // open: gt, lt

  assign Signed_Overflow = 1'b0;

  // Notes on the sheet:
  //   INPUTS to your circuit
  //   OUTPUTS from your circuit
endmodule

module srl (
  input  [31:0] X,
  input  [31:0] Y,
  output Signed_Overflow,
  output Equal,
  output [31:0] Result
);

  Shifter #(.width(32), .shift("lr")) shifter_1 (.in(Y), .\dist (X[4:0]), .out(Result));
  Comparator #(.width(32)) comparator_1 (.a(Y), .b(X), .eq(Equal));  // open: gt, lt

  assign Signed_Overflow = 1'b0;

  // Notes on the sheet:
  //   INPUTS to your circuit
  //   OUTPUTS from your circuit
endmodule

module sra (
  input  [31:0] X,
  input  [31:0] Y,
  output Signed_Overflow,
  output Equal,
  output [31:0] Result
);

  Shifter #(.width(32), .shift("ar")) shifter_1 (.in(Y), .\dist (X[4:0]), .out(Result));
  Comparator #(.width(32)) comparator_1 (.a(Y), .b(X), .eq(Equal));  // open: gt, lt

  assign Signed_Overflow = 1'b0;

  // Notes on the sheet:
  //   INPUTS to your circuit
  //   OUTPUTS from your circuit
endmodule

module add (
  input  [31:0] X,
  input  [31:0] Y,
  output Signed_Overflow,
  output Equal,
  output [31:0] Result
);

  wire and_1_out, and_2_out, not_1_out, not_2_out, not_3_out;

  not not_1 (not_1_out, Result[31]);
  not not_2 (not_2_out, X[31]);
  not not_3 (not_3_out, Y[31]);
  Adder #(.width(32)) adder_1 (.a(X), .b(Y), .out(Result));  // open: cin, cout
  Comparator #(.width(32)) comparator_1 (.a(X), .b(Y), .eq(Equal));  // open: gt, lt
  and and_1 (and_1_out, X[31], Y[31], not_1_out);
  and and_2 (and_2_out, not_2_out, not_3_out, Result[31]);
  or or_1 (Signed_Overflow, and_1_out, and_2_out);

  // Notes on the sheet:
  //   INPUTS to your circuit
  //   OUTPUTS from your circuit
endmodule

module addu (
  input  [31:0] X,
  input  [31:0] Y,
  output Signed_Overflow,
  output Equal,
  output [31:0] Result
);

  Adder #(.width(32)) adder_1 (.a(X), .b(Y), .out(Result));  // open: cin, cout
  Comparator #(.width(32)) comparator_1 (.a(X), .b(Y), .eq(Equal));  // open: gt, lt

  assign Signed_Overflow = 1'b0;

  // Notes on the sheet:
  //   INPUTS to your circuit
  //   OUTPUTS from your circuit
endmodule

module sub (
  input  [31:0] X,
  input  [31:0] Y,
  output Signed_Overflow,
  output Equal,
  output [31:0] Result
);

  wire and_1_out, and_2_out, not_1_out, not_2_out, not_3_out;
  wire [31:0] negator_1_out;

  Negator #(.width(32)) negator_1 (.in(Y), .out(negator_1_out));
  not not_1 (not_1_out, Result[31]);
  not not_2 (not_2_out, X[31]);
  not not_3 (not_3_out, negator_1_out[31]);
  and and_1 (and_1_out, X[31], negator_1_out[31], not_1_out);
  and and_2 (and_2_out, not_2_out, not_3_out, Result[31]);
  Subtractor #(.width(32)) subtractor_1 (.a(X), .b(Y), .out(Result));  // open: bin, bout
  Comparator #(.width(32)) comparator_1 (.a(X), .b(Y), .eq(Equal));  // open: gt, lt
  or or_1 (Signed_Overflow, and_1_out, and_2_out);

  // Notes on the sheet:
  //   INPUTS to your circuit
  //   OUTPUTS from your circuit
endmodule

module subu (
  input  [31:0] X,
  input  [31:0] Y,
  output Signed_Overflow,
  output Equal,
  output [31:0] Result
);

  wire [31:0] negator_1_out;

  Negator #(.width(32)) negator_1 (.in(Y), .out(negator_1_out));
  Adder #(.width(32)) adder_1 (.a(X), .b(negator_1_out), .out(Result));  // open: cin, cout
  Comparator #(.width(32)) comparator_1 (.a(X), .b(Y), .eq(Equal));  // open: gt, lt

  assign Signed_Overflow = 1'b0;

  // Notes on the sheet:
  //   INPUTS to your circuit
  //   OUTPUTS from your circuit
endmodule

module \and  (
  input  [31:0] X,
  input  [31:0] Y,
  output Signed_Overflow,
  output Equal,
  output [31:0] Result
);

  assign Result = X & Y;  // AND_Gate and_1, 32 bits wide
  Comparator #(.width(32)) comparator_1 (.a(X), .b(Y), .eq(Equal));  // open: gt, lt

  assign Signed_Overflow = 1'b0;

  // Notes on the sheet:
  //   INPUTS to your circuit
  //   OUTPUTS from your circuit
endmodule

module \or  (
  input  [31:0] X,
  input  [31:0] Y,
  output Signed_Overflow,
  output Equal,
  output [31:0] Result
);

  Comparator #(.width(32)) comparator_1 (.a(X), .b(Y), .eq(Equal));  // open: gt, lt
  assign Result = X | Y;  // OR_Gate or_1, 32 bits wide

  assign Signed_Overflow = 1'b0;

  // Notes on the sheet:
  //   INPUTS to your circuit
  //   OUTPUTS from your circuit
endmodule

module \xor  (
  input  [31:0] X,
  input  [31:0] Y,
  output Signed_Overflow,
  output Equal,
  output [31:0] Result
);

  Comparator #(.width(32)) comparator_1 (.a(X), .b(Y), .eq(Equal));  // open: gt, lt
  assign Result = X ^ Y;  // XOR_Gate xor_1, 32 bits wide

  assign Signed_Overflow = 1'b0;

  // Notes on the sheet:
  //   INPUTS to your circuit
  //   OUTPUTS from your circuit
endmodule

module slt (
  input  [31:0] X,
  input  [31:0] Y,
  output Signed_Overflow,
  output Equal,
  output [31:0] Result
);

  Comparator #(.width(32)) comparator_1 (.a(X), .b(Y), .eq(Equal), .lt(Result[0]));  // open: gt

  assign Result[31:1] = {31{1'b0}};
  assign Signed_Overflow = 1'b0;

  // Notes on the sheet:
  //   INPUTS to your circuit
  //   OUTPUTS from your circuit
endmodule

module sltu (
  input  [31:0] X,
  input  [31:0] Y,
  output Signed_Overflow,
  output Equal,
  output [31:0] Result
);

  Comparator #(.width(32), .mode("unsigned")) comparator_1 (.a(X), .b(Y), .eq(Equal), .lt(Result[0]));  // open: gt

  assign Result[31:1] = {31{1'b0}};
  assign Signed_Overflow = 1'b0;

  // Notes on the sheet:
  //   INPUTS to your circuit
  //   OUTPUTS from your circuit
endmodule
