// Logisim project cpu.circ as structural Verilog: 5 circuits, main circuit main
module main (
  input  [31:0] INSTRUCTION,
  input  CLOCK,
  output [31:0] FETCH_ADDRESS,
  output [31:0] s0_Value,
  output [31:0] s1_Value,
  output [31:0] s2_Value,
  output [31:0] ra_Value,
  output [31:0] sp_Value
);

  wire alusrc, controlunit_1_branch, mem_to_reg, memtoreg, memwrite, pc_src, regdst, regwrite, zero;
  wire [3:0] alucontrol;
  wire [4:0] multiplexer_1_out;
  wire [23:0] bit_extender_2_out;
  wire [31:0] imm, main_1_result, multiplexer_2_out, multiplexer_3_out, ram_1_data, RegisterFile_read1,
       RegisterFile_read2;

  Multiplexer #(.width(5)) multiplexer_1 (
    .in0(INSTRUCTION[20:16]), .in1(INSTRUCTION[15:11]), .out(multiplexer_1_out), .sel(regwrite));  // open: en
  pc_control pc_control_1 (.instruction(INSTRUCTION), .imm(imm), .pc_src(pc_src), .fetch_addr(FETCH_ADDRESS));
  regfile RegisterFile (
    .write_register(multiplexer_1_out), .write_enable(regwrite), .in_4(multiplexer_3_out),
    .read_register_1(INSTRUCTION[25:21]), .Read1(RegisterFile_read1), .read_register_2(INSTRUCTION[20:16]),
    .Read2(RegisterFile_read2), .ra(sp_Value), .sp(ra_Value), .S2(s2_Value), .S1(s1_Value), .S0(s0_Value),
    .clock(CLOCK));
  assign imm = {{16{INSTRUCTION[15]}}, INSTRUCTION[15:0]};  // Bit_Extender bit_extender_1
  ControlUnit controlunit_1 (
    .Opcode(INSTRUCTION[5:0]), .Funct(INSTRUCTION[31:26]), .RegWrite(regwrite), .RegDst(regdst),
    .ALUSrc(alusrc), .Branch(controlunit_1_branch), .MemWrite(memwrite), .MemToReg(memtoreg),
    .ALUControl(alucontrol[2:0]));
  Multiplexer #(.width(32)) multiplexer_2 (
    .in0(RegisterFile_read2), .in1(imm), .out(multiplexer_2_out), .sel(alusrc));  // open: en
  alu_main main_1 (
    .Switch(alucontrol), .X(RegisterFile_read1), .Equal(zero), .Result(main_1_result), .Y(multiplexer_2_out));  // open: Signed_Overflow
  Bit_Extender #(.in_width(32), .out_width(24)) bit_extender_2 (.in(main_1_result), .out(bit_extender_2_out));
  and and_1 (pc_src, zero, controlunit_1_branch);
  RAM #(.addrWidth(24), .dataWidth(32), .bus("separate")) ram_1 (
    .addr(bit_extender_2_out), .din(RegisterFile_read2), .data(ram_1_data), .str(memwrite), .clk(CLOCK),
    .ld(1'b1));  // open: sel, clr
  Multiplexer #(.width(32)) multiplexer_3 (
    .in0(main_1_result), .in1(ram_1_data), .out(multiplexer_3_out), .sel(mem_to_reg));  // open: en
  // Pins of 3 and 4 bits meet at alucontrol

  // Other names for the same wires on the sheet: clk = CLOCK; fetch_addr[31:0] = FETCH_ADDRESS;
  //   opcode[5:0] = INSTRUCTION[5:0]; funct[5:0] = INSTRUCTION[31:26]; ra[31:0] = ra_Value; s0[31:0] = s0_Value;
  //   s1[31:0] = s1_Value; s2[31:0] = s2_Value; sp[31:0] = sp_Value

  // Notes on the sheet:
  //   Output
  //   PC Control
  //   These are outputs/inputs from run.circ
  //   Inputs
  //   These are DEBUG/TEST outputs from your circuit.
  //   Control Unit
endmodule

module pc_control (
  input  [31:0] instruction,
  input  [31:0] imm,
  input  pc_src,
  output [31:0] fetch_addr
);

  wire [31:0] adder_1_out, adder_2_out, shifter_1_out;

  Adder #(.width(32)) adder_1 (.a(instruction), .b(32'h4), .out(adder_1_out));  // open: cin, cout
  Adder #(.width(32)) adder_2 (.a(adder_1_out), .b(shifter_1_out), .out(adder_2_out));  // open: cin, cout
  Shifter #(.width(32)) shifter_1 (.in(imm), .\dist (5'b00010), .out(shifter_1_out));
  Multiplexer #(.width(32)) multiplexer_1 (
    .in0(adder_1_out), .in1(adder_2_out), .out(fetch_addr), .sel(pc_src));  // open: en
endmodule

module ControlUnit (
  input  [5:0] Opcode,
  input  [5:0] Funct,
  output RegWrite,
  output RegDst,
  output ALUSrc,
  output Branch,
  output MemWrite,
  output MemToReg,
  output [2:0] ALUControl
);

  wire and_1_out, and_2_out, and_4_out, and_5_out, and_6_out, and_7_out, not_1_out, not_2_out, not_4_out,
       not_5_out, not_6_out, not_7_out, not_8_out;
  wire [0:0] ALUOp;

  not not_1 (not_1_out, Opcode[3]);
  not not_2 (not_2_out, Opcode[2]);
  not not_3 (RegDst, Opcode[1]);
  not not_4 (not_4_out, Opcode[5]);
  not not_5 (not_5_out, Opcode[2]);
  and and_1 (and_1_out, not_1_out, not_2_out);
  or or_1 (RegWrite, and_1_out, and_2_out);
  and and_2 (and_2_out, Opcode[3], Opcode[2]);
  and and_3 (ALUOp[0], not_4_out, not_5_out);
  not not_6 (not_6_out, Funct[5]);
  not not_7 (not_7_out, ALUOp[0]);
  not not_8 (not_8_out, Funct[2]);
  and and_4 (and_4_out, ALUOp[0], Funct[0]);
  and and_5 (and_5_out, ALUOp[0], Funct[3]);
  and and_6 (and_6_out, ALUOp[0], not_6_out);
  and and_7 (and_7_out, ALUOp[0], Funct[1]);
  or or_2 (ALUControl[1], not_7_out, not_8_out);
  or or_3 (ALUControl[0], and_4_out, and_5_out);
  or or_4 (ALUControl[2], Opcode[2], and_6_out, and_7_out);

  assign ALUSrc = Opcode[0];
  assign Branch = Opcode[2];
  assign MemToReg = Opcode[0];
  assign MemWrite = Opcode[3];

  // Other names for the same wires on the sheet: ALUOp[1] = Opcode[2]
endmodule

module Decoder (
  input  Opcode,
  input  Opcode2,
  input  Opcode3,
  input  Opcode4,
  input  Opcode5,
  input  Opcode6,
  output RegWrite,
  output RegDst,
  output ALUSrc,
  output Branch,
  output MemWrite,
  output MemToReg,
  output ALUOp,
  output ALUOp2
);

  wire and_1_out, and_2_out, not_1_out, not_2_out, not_4_out, not_5_out;

  not not_1 (not_1_out, Opcode3);
  not not_2 (not_2_out, Opcode4);
  not not_3 (RegDst, Opcode5);
  not not_4 (not_4_out, Opcode);
  not not_5 (not_5_out, Opcode4);
  and and_1 (and_1_out, not_1_out, not_2_out);
  and and_2 (and_2_out, Opcode3, Opcode4);
  and and_3 (ALUOp, not_4_out, not_5_out);
  or or_1 (RegWrite, and_1_out, and_2_out);

  assign ALUOp2 = Opcode4;
  assign ALUSrc = Opcode6;
  assign Branch = Opcode4;
  assign MemToReg = Opcode6;
  assign MemWrite = Opcode3;
endmodule

module ALUDecoder (
  input  ALUOp1,
  input  ALUOp2,
  input  Funct1,
  input  Funct2,
  input  Funct3,
  input  Funct4,
  input  Funct5,
  input  Funct6,
  output AluControl1,
  output AluControl2,
  output AluControl3
);

  wire and_1_out, and_2_out, and_3_out, and_4_out, not_1_out, not_2_out, not_3_out;

  and and_1 (and_1_out, ALUOp1, not_1_out);
  not not_1 (not_1_out, Funct1);
  and and_2 (and_2_out, ALUOp1, Funct5);
  not not_2 (not_2_out, ALUOp1);
  or or_1 (AluControl2, not_2_out, not_3_out);
  not not_3 (not_3_out, Funct4);
  and and_3 (and_3_out, ALUOp1, Funct6);
  and and_4 (and_4_out, ALUOp1, Funct3);
  or or_2 (AluControl1, ALUOp2, and_1_out, and_2_out);
  or or_3 (AluControl3, and_3_out, and_4_out);
endmodule
