// Logisim project regfile.circ as structural Verilog: 3 circuits, main circuit main
module main (
  input  [4:0] Read_Register_1,
  input  [4:0] Read_Register_2,
  input  [4:0] Write_Register,
  input  [31:0] Write_Data,
  input  Write_Enable,
  input  Clock,
  output [31:0] s0_Value,
  output [31:0] s1_Value,
  output [31:0] s2_Value,
  output [31:0] ra_Value,
  output [31:0] sp_Value,
  output [31:0] Read_Data_1,
  output [31:0] Read_Data_2
);

  regfile regfile_1 (
    .write_register(Write_Register), .write_enable(Write_Enable), .wIn(Write_Data),
    .read_register_1(Read_Register_1), .Read1(Read_Data_1), .read_register_2(Read_Register_2),
    .Read2(Read_Data_2), .ra(ra_Value), .sp(sp_Value), .S2(s2_Value), .S1(s1_Value), .S0(s0_Value),
    .clock(Clock));

  // Other names for the same wires on the sheet: clk = Clock; read_data1[31:0] = Read_Data_1;
  //   read_data2[31:0] = Read_Data_2; read_reg1[4:0] = Read_Register_1; read_reg2[4:0] = Read_Register_2;
  //   write_en = Write_Enable; write_reg[4:0] = Write_Register

  // Notes on the sheet:
  //   INPUTS to your circuit
  //   DON'T CHANGE THE LOCATIONS OF THE INPUTS AND OUTPUTS!
  //   These are DEBUG/TEST outputs from your circuit.
  //   OUTPUTS from your circuit
endmodule

module gated_register (
  input  [31:0] \input ,
  input  wenable,
  input  clock,
  output [31:0] \output 
);

  wire [31:0] multiplexer_1_out;

  Multiplexer #(.width(32)) multiplexer_1 (
    .in0(\output ), .in1(\input ), .out(multiplexer_1_out), .sel(wenable));  // open: en
  Register #(.width(32)) register_1 (.D(multiplexer_1_out), .Q(\output ), .clk(clock));  // open: en, clr

  // Notes on the sheet:
  //   Stores Input in the register if wenable is set to 0 on clock up
endmodule

module regfile (
  input  [4:0] read_register_2,
  input  [4:0] read_register_1,
  input  clock,
  input  [31:0] wIn,
  input  [4:0] write_register,
  input  write_enable,
  output [31:0] ra,
  output [31:0] sp,
  output [31:0] S2,
  output [31:0] S1,
  output [31:0] S0,
  output [31:0] Read1,
  output [31:0] Read2
);

  wire decoder_1_out1, decoder_1_out2, decoder_1_out3, decoder_1_out4, decoder_1_out5, decoder_1_out6,
       decoder_1_out7, decoder_1_out8, decoder_1_out9, decoder_1_out10, decoder_1_out11, decoder_1_out12,
       decoder_1_out13, decoder_1_out14, decoder_1_out15, decoder_1_out16, decoder_1_out17, decoder_1_out18,
       decoder_1_out19, decoder_1_out20, decoder_1_out21, decoder_1_out22, decoder_1_out23, decoder_1_out24,
       decoder_1_out25, decoder_1_out26, decoder_1_out27, decoder_1_out28, decoder_1_out29, decoder_1_out30,
       decoder_1_out31;
  wire [31:0] _1_out, _2_out, _3_out, _4_out, _5_out, _6_out, _7_out, _8_out, _9_out, _10_out, _11_out,
       _12_out, _13_out, _14_out, _15_out, _19_out, _20_out, _21_out, _22_out, _23_out, _24_out, _25_out,
       _26_out, _27_out, _28_out, _30_out;

  gated_register _1 (.\input (wIn), .wenable(decoder_1_out1), .clock(clock), .\output (_1_out));
  gated_register _2 (.\input (wIn), .wenable(decoder_1_out2), .clock(clock), .\output (_2_out));
  gated_register _3 (.\input (wIn), .wenable(decoder_1_out3), .clock(clock), .\output (_3_out));
  gated_register _4 (.\input (wIn), .wenable(decoder_1_out4), .clock(clock), .\output (_4_out));
  gated_register _5 (.\input (wIn), .wenable(decoder_1_out5), .clock(clock), .\output (_5_out));
  gated_register _6 (.\input (wIn), .wenable(decoder_1_out6), .clock(clock), .\output (_6_out));
  gated_register _7 (.\input (wIn), .wenable(decoder_1_out7), .clock(clock), .\output (_7_out));
  gated_register _8 (.\input (wIn), .wenable(decoder_1_out8), .clock(clock), .\output (_8_out));
  gated_register _9 (.\input (wIn), .wenable(decoder_1_out9), .clock(clock), .\output (_9_out));
  gated_register _10 (.\input (wIn), .wenable(decoder_1_out10), .clock(clock), .\output (_10_out));
  gated_register _11 (.\input (wIn), .wenable(decoder_1_out11), .clock(clock), .\output (_11_out));
  Decoder #(.select(5), .disabled(0)) decoder_1 (
    .out1(decoder_1_out1), .out2(decoder_1_out2), .out3(decoder_1_out3), .out4(decoder_1_out4),
    .out5(decoder_1_out5), .out6(decoder_1_out6), .out7(decoder_1_out7), .out8(decoder_1_out8),
    .out9(decoder_1_out9), .out10(decoder_1_out10), .out11(decoder_1_out11), .out12(decoder_1_out12),
    .out13(decoder_1_out13), .out14(decoder_1_out14), .out15(decoder_1_out15), .out16(decoder_1_out16),
    .out17(decoder_1_out17), .out18(decoder_1_out18), .out19(decoder_1_out19), .out20(decoder_1_out20),
    .out21(decoder_1_out21), .out22(decoder_1_out22), .out23(decoder_1_out23), .out24(decoder_1_out24),
    .out25(decoder_1_out25), .out26(decoder_1_out26), .out27(decoder_1_out27), .out28(decoder_1_out28),
    .out29(decoder_1_out29), .out30(decoder_1_out30), .out31(decoder_1_out31), .sel(write_register),
    .en(write_enable));  // open: out0
  gated_register _12 (.\input (wIn), .wenable(decoder_1_out12), .clock(clock), .\output (_12_out));
  gated_register _13 (.\input (wIn), .wenable(decoder_1_out13), .clock(clock), .\output (_13_out));
  gated_register _14 (.\input (wIn), .wenable(decoder_1_out14), .clock(clock), .\output (_14_out));
  gated_register _15 (.\input (wIn), .wenable(decoder_1_out15), .clock(clock), .\output (_15_out));
  gated_register _16 (.\input (wIn), .wenable(decoder_1_out16), .clock(clock), .\output (S0));
  gated_register _17 (.\input (wIn), .wenable(decoder_1_out17), .clock(clock), .\output (S1));
  gated_register _18 (.\input (wIn), .wenable(decoder_1_out18), .clock(clock), .\output (S2));
  gated_register _19 (.\input (wIn), .wenable(decoder_1_out19), .clock(clock), .\output (_19_out));
  gated_register _20 (.\input (wIn), .wenable(decoder_1_out20), .clock(clock), .\output (_20_out));
  gated_register _21 (.\input (wIn), .wenable(decoder_1_out21), .clock(clock), .\output (_21_out));
  gated_register _22 (.\input (wIn), .wenable(decoder_1_out22), .clock(clock), .\output (_22_out));
  gated_register _23 (.\input (wIn), .wenable(decoder_1_out23), .clock(clock), .\output (_23_out));
  gated_register _24 (.\input (wIn), .wenable(decoder_1_out24), .clock(clock), .\output (_24_out));
  gated_register _25 (.\input (wIn), .wenable(decoder_1_out25), .clock(clock), .\output (_25_out));
  gated_register _26 (.\input (wIn), .wenable(decoder_1_out26), .clock(clock), .\output (_26_out));
  gated_register _27 (.\input (wIn), .wenable(decoder_1_out27), .clock(clock), .\output (_27_out));
  gated_register _28 (.\input (wIn), .wenable(decoder_1_out28), .clock(clock), .\output (_28_out));
  gated_register _29 (.\input (wIn), .wenable(decoder_1_out29), .clock(clock), .\output (sp));
  gated_register _30 (.\input (wIn), .wenable(decoder_1_out30), .clock(clock), .\output (_30_out));
  gated_register _31 (.\input (wIn), .wenable(decoder_1_out31), .clock(clock), .\output (ra));
  Multiplexer #(.select(5), .width(32)) multiplexer_1 (
    .in0({32{1'b0}}), .in1(_1_out), .in2(_2_out), .in3(_3_out), .in4(_4_out), .in5(_5_out), .in6(_6_out),
    .in7(_7_out), .in8(_8_out), .in9(_9_out), .in10(_10_out), .in11(_11_out), .in12(_12_out), .in13(_13_out),
    .in14(_14_out), .in15(_15_out), .in16(S0), .in17(S1), .in18(S2), .in19(_19_out), .in20(_20_out),
    .in21(_21_out), .in22(_22_out), .in23(_23_out), .in24(_24_out), .in25(_25_out), .in26(_26_out),
    .in27(_27_out), .in28(_28_out), .in29(sp), .in30(_30_out), .in31(ra), .out(Read1), .sel(read_register_1));  // open: en
  Multiplexer #(.select(5), .width(32)) multiplexer_2 (
    .in0({32{1'b0}}), .in1(_1_out), .in2(_2_out), .in3(_3_out), .in4(_4_out), .in5(_5_out), .in6(_6_out),
    .in7(_7_out), .in8(_8_out), .in9(_9_out), .in10(_10_out), .in11(_11_out), .in12(_12_out), .in13(_13_out),
    .in14(_14_out), .in15(_15_out), .in16(S0), .in17(S1), .in18(S2), .in19(_19_out), .in20(_20_out),
    .in21(_21_out), .in22(_22_out), .in23(_23_out), .in24(_24_out), .in25(_25_out), .in26(_26_out),
    .in27(_27_out), .in28(_28_out), .in29(sp), .in30(_30_out), .in31(ra), .out(Read2), .sel(read_register_2));  // open: en

  // Other names for the same wires on the sheet: _16_out[31:0] = S0; _17_out[31:0] = S1; _18_out[31:0] = S2;
  //   _29_out[31:0] = sp; _31_out[31:0] = ra
endmodule
